# Fritzing sketch Schaltung (saved by Fritzing 0.9.9b)
breadboards: 1

parts:
  WeMos_D1_Mini1 = WeMos D1 Mini
  R1 = PHOTOCELL [package=photocell]
  RE1 = Rotary Encoder [package=THT]
  R2 = Resistor [tolerance=±5% power=0.25 resistance=220 package=THT]
  Mod1 = KY-019 5V Relay Module [package="Breakout board"]
  Mod2 = KY-019 5V Relay Module [package="Breakout board"]

nets:
  N1: WeMos_D1_Mini1.5V, R1.P$2, Mod1.-, Mod2.-
  N2: WeMos_D1_Mini1.A0, R2.Pin_0
  N3: WeMos_D1_Mini1.G, Mod1.+, Mod2.+
  N4: R1.P$1, RE1.EncoderPinC
  N5: RE1.EncoderPinA, R2.Pin_1

custom parts:
  KY-019 5V Relay Module: KY-019 5V Relay module, used to control AC circuits. (Special thanks to vanepp for fixing the PCB holes and other errors)
